# Fritzing sketch raspi-ruxpin (saved by Fritzing 0.9.9b)
breadboards: 1

parts:
  Raspberry_Pi_1 = Raspberry Pi 3 [part_number=RPI-3-V1.2]
  Part1 = Motor Driver 1A Dual TB6612FNG  # not connected
  M1 = DC Motor
  M2 = DC Motor
  M3 = DC Motor  # not connected
  J1 = Power Jack [package=power_jack_pth]

nets:
  GND: Raspberry_Pi_1.GND, J1.GND, J1.GNDBREAK
  N1: Raspberry_Pi_1.5V, J1.PWR
  N2: M1.pin_1, M2.pin_1
  N3: M1.pin_2, M2.pin_2

notes:
  upper lip
  lower lip
  eyes
